# Fritzing sketch ESQUEMA PAPELERA (saved by Fritzing 0.9.3b)
breadboards: 1

parts:
  R1 = Rotary Potentiometer (Small) [maximum_resistance=100kΩ package=THT]
  hc-sr1 = hc-sr04
  U1 = LCD-16X2 [package=lcd-16x2_noholes]
  Componente1 = Arduino Uno (Rev3)
  R2 = Resistor [tolerance=±5% resistance=220 package=THT]
  T1 = LM35 Temperature Sensor [package="TO92 [THT]"]
  Componente2 = Real Time Clock Module - DS1307 RTC Breakout Board

nets:
  VCC: R1.leg1, hc-sr1.VCC, U1.VDD, Componente2.5V
  N1: R1.wiper, U1.VO
  GND: R1.leg2, hc-sr1.GND, U1.VSS, U1.R_W, Componente2.GND
  N2: hc-sr1.Trig, Componente1.D10_PWM/SS
  N3: hc-sr1.Echo, Componente1.D6_PWM
  N4: U1.RS, Componente1.D12/MISO
  N5: U1.E, Componente1.D11_PWM/MOSI
  N6: U1.DB4, Componente1.D5_PWM
  N7: U1.DB5, Componente1.D4
  N8: U1.DB6, Componente1.D3_PWM
  N9: U1.DB7, Componente1.D2
  N10: U1.A, R2.Pin_0
  N11: Componente1.A0, T1.Vout
  N12: Componente1.A4/SDA, Componente2.SQW
  N13: Componente1.A5/SCL, Componente2.SCL
  N14: R2.Pin_1, T1.GND
